# Fritzing sketch Circuit (saved by Fritzing 0.9.3b)
breadboards: 1

parts:
  Part1 = Arduino Uno (Rev3)
  S1 = Momentary Switch [package=ksa_sealed_tac_switch]
  S2 = Momentary Switch [package=ksa_sealed_tac_switch]
  LED1 = LED - 5mm [color="Red (633nm)" package="5 mm [THT]"]
  LED2 = LED - 5mm [color="Red (633nm)" package="5 mm [THT]"]
  R1 = Resistor [tolerance=±5% resistance=220 package=THT]
  R2 = Resistor [tolerance=±5% resistance=220 package=THT]

nets:
  N1: Part1.D8, R1.Pin_0
  N2: Part1.D9_PWM, S1.1, S1.3
  N3: Part1.D10_PWM/SS, R2.Pin_0
  N4: Part1.D11_PWM/MOSI, S2.1, S2.3
  N5: Part1.5V, S1.2, S1.4, S2.2, S2.4
  N6: Part1.GND, LED1.anode, LED2.anode
  N7: LED1.cathode, R2.Pin_1
  N8: LED2.cathode, R1.Pin_1
